# Fritzing sketch ataribreakout (saved by Fritzing 0.9.3b)
breadboards: 2

parts:
  Part1 = Arduino Mega 2560 (Rev3)
  Disp1 = LBT2088AH [part_number=LBT2088AH]
  S2 = Momentary Switch [package=ksa_sealed_tac_switch]
  S3 = Momentary Switch [package=ksa_sealed_tac_switch]
  R1 = Resistor [tolerance=±5% resistance=220 package="2010 [SMD]"]
  R2 = Resistor [tolerance=±5% resistance=220 package="2010 [SMD]"]

nets:
  N1: Part1.GND, R1.Pin_0, R2.Pin_0
  N2: Part1.D10_PWM, S2.2
  N3: Part1.5V, S2.3, S3.1
  N4: Part1.D22, Disp1.pin_9
  N5: Part1.D23, Disp1.pin_14
  N6: Part1.D24, Disp1.pin_8
  N7: Part1.D25, Disp1.pin_12
  N8: Part1.D26, Disp1.pin1
  N9: Part1.D27, Disp1.pin_7
  N10: Part1.D28, Disp1.pin2
  N11: Part1.D29, Disp1.pin_5
  N12: Part1.D30, Disp1.pin_16
  N13: Part1.D31, Disp1.pin_15
  N14: Part1.D32, Disp1.pin_11
  N15: Part1.D33, Disp1.pin_6
  N16: Part1.D34, Disp1.pin_10
  N17: Part1.D35, Disp1.pin_4
  N18: Part1.D36, Disp1.pin_3
  N19: Part1.D37, Disp1.pin_13
  N20: Part1.D41, S3.4
  N21: S2.1, R2.Pin_1
  N22: S3.3, R1.Pin_1
